# Fritzing sketch schematic (saved by Fritzing 1.0.3b)
breadboards: 1

parts:
  TMC2240-1 = IC, DIP package, 16 pins [chip_label=IC]
  TMC2240-2 = IC, DIP package, 16 pins [chip_label=IC]
  TMC2240-3 = IC, DIP package, 16 pins [chip_label=IC]
  TMC2240-4 = IC, DIP package, 16 pins [chip_label=IC]
  part = ESP-WROOM-32 [ESP-32S] Module [part_number=ESP-WROOM-32]
  Home-1 = LJ18A3-H-ZBX [package=THT]
  Home-2 = LJ18A3-H-ZBX [package=THT]
  Home-3 = LJ18A3-H-ZBX [package=THT]
  Home-4 = LJ18A3-H-ZBX [package=THT]

nets:
  N1: TMC2240-1.pin1, part.IO14
  N2: TMC2240-1.pin4, part.IO22
  MISO: TMC2240-1.pin5, TMC2240-2.pin5, TMC2240-3.pin5, TMC2240-4.pin5, part.IO19
  N3: TMC2240-1.pin7, part.IO33
  N4: TMC2240-1.pin8, part.IO16
  GND: TMC2240-1.pin9, TMC2240-1.pin15, TMC2240-2.pin9, TMC2240-2.pin15, TMC2240-3.pin9, TMC2240-3.pin15, TMC2240-4.pin9, TMC2240-4.pin15, Home-1.VO_(BLU), Home-2.VO_(BLU), Home-3.VO_(BLU), Home-4.VO_(BLU)
  5V: TMC2240-1.pin10, TMC2240-2.pin10, TMC2240-3.pin10, TMC2240-4.pin10, Home-1.VI_(BRN), Home-2.VI_(BRN), Home-3.VI_(BRN), Home-4.VI_(BRN)
  24V: TMC2240-1.pin16, TMC2240-2.pin16, TMC2240-3.pin16, TMC2240-4.pin16
  N5: TMC2240-2.pin1, part.IO12
  MOSI: TMC2240-2.pin2, TMC2240-3.pin2, TMC2240-4.pin2, part.IO23
  SCK: TMC2240-2.pin3, TMC2240-3.pin3, TMC2240-4.pin3, part.IO18
  N6: TMC2240-2.pin4, part.IO21
  N7: TMC2240-2.pin7, part.IO25
  N8: TMC2240-2.pin8, part.IO4
  N9: TMC2240-3.pin1, part.IO13
  N10: TMC2240-3.pin4, part.IO20
  N11: TMC2240-3.pin7, part.IO26
  N12: TMC2240-3.pin8, part.IO2
  N13: TMC2240-4.pin1, part.IO5
  N14: TMC2240-4.pin4, part.IO17
  N15: TMC2240-4.pin7, part.IO27
  N16: TMC2240-4.pin8, part.IO15
  N17: part.SVP, Home-1.SIG_(BLK)
  N18: part.SVN, Home-2.SIG_(BLK)
  N19: part.IO34, Home-3.SIG_(BLK)
  N20: part.IO35, Home-4.SIG_(BLK)

custom parts:
  ESP-WROOM-32 [ESP-32S] Module: Espressif ESP-WROOM-32 WiFi/Bluetooth LE microcontroller module also known as the Ai-Thinker ESP-32S module with similar formfactor. The ESP32 is a microcontroller chip with WiFi and BLE capabilities. The chip is developed by Espressif and is the successor to the popular ESP8266 WiFi module.
  LJ18A3-H-ZBX: LJ18A3-H-ZBX Proximity Sensor module.
